# Fritzing sketch circuitDiagram (saved by Fritzing 0.9.3b)
breadboards: 1

parts:
  U1 = NodeMCU V1.0
  J1 = Basic Servo
  U2 = LCD-16X2 [package=lcd-16x2_noholes]
  Part2 = KY-037 High Sensitivity Sound Detection Module [package="Breakout board"]
  Part3 = RFID-RC522-v2
  LCM1602_IIC1 = LCM1602 IIC [part_number="LCM1602 IIC" chip_label="LCM1602 IIC" package="DIP (Dual Inline) [THT]"]
  S1 = Momentary Switch [package=ksa_sealed_tac_switch]

nets:
  N1: U1.D0, Part3.RST
  N2: U1.D1, LCM1602_IIC1.SCL
  N3: U1.D2, LCM1602_IIC1.SDA
  N4: U1.D3, J1.pulse
  N5: U1.D4, S1.1
  3V3: U1.3V3, J1.vcc, Part2.+, Part3.3_3V
  GND: U1.GND, J1.gnd, Part2.G, Part3.GND, LCM1602_IIC1.GND, S1.4
  N6: U1.D5, Part3.SCK
  N7: U1.D6, Part3.MISO
  N8: U1.D7, Part3.MOSI
  N9: U1.D8, Part3.SDA
  VIN: U1.Vin, LCM1602_IIC1.VCC
  N10: U1.A0, Part2.A0
  VSS: U2.VSS, LCM1602_IIC1.VSS
  VDD: U2.VDD, LCM1602_IIC1.VDD
  N11: U2.VO, LCM1602_IIC1.V0
  N12: U2.RS, LCM1602_IIC1.RS
  N13: U2.R_W, LCM1602_IIC1.RW
  N14: U2.E, LCM1602_IIC1.E
  N15: U2.DB0, LCM1602_IIC1.D0
  N16: U2.DB1, LCM1602_IIC1.D1
  N17: U2.DB2, LCM1602_IIC1.D2
  N18: U2.DB3, LCM1602_IIC1.D3
  N19: U2.DB4, LCM1602_IIC1.D4
  N20: U2.DB5, LCM1602_IIC1.D5
  N21: U2.DB6, LCM1602_IIC1.D6
  N22: U2.DB7, LCM1602_IIC1.D7
  N23: U2.A, LCM1602_IIC1.A
  N24: U2.K, LCM1602_IIC1.K

custom parts:
  NodeMCU V1.0: ESP8266 based NodeMCU
  KY-037 High Sensitivity Sound Detection Module: KY-037 high sensitivity sound detection module is an analog/digital sensor that uses a condenser microphone to observe changes in environment noise.
  RFID-RC522-v2: A simple China made RFID-RC522 Reader; do check the pin labels, as this is a MFRC522 based clone.
  LCM1602 IIC: I2C-Module to use a 1602 or 2004 LCD on with the wire.h libory Serial LCD Modul
